// Logisim project nono_1.circ as structural Verilog: 8 circuits, main circuit Nono-1
module UAL (
  input  [7:0] Rs,
  input  [7:0] Rt,
  input  [2:0] ctrUAL,
  output [7:0] Res,
  output [3:0] CF_OF_SF_ZF
);

  wire adder_1_cout, subtractor_1_bout, undriven;
  wire [7:0] adder_1_out, and_1_out, not_1_out, or_1_out, shifter_1_out, shifter_2_out, subtractor_1_out;

  Adder adder_1 (.a(Rs), .b(Rt), .out(adder_1_out), .cout(adder_1_cout));  // open: cin
  Subtractor subtractor_1 (.a(Rs), .b(Rt), .out(subtractor_1_out), .bout(subtractor_1_bout));  // open: bin
  assign or_1_out = Rs | Rt;  // OR_Gate or_1, 8 bits wide
  assign and_1_out = Rs & Rt;  // AND_Gate and_1, 8 bits wide
  assign not_1_out = ~Rs;  // NOT_Gate not_1, 8 bits wide
  Shifter shifter_1 (.in(Rs), .\dist (Rt[2:0]), .out(shifter_1_out));
  Shifter #(.shift("lr")) shifter_2 (.in(Rs), .\dist (Rt[2:0]), .out(shifter_2_out));
  and OF (CF_OF_SF_ZF[2], Rs[7], undriven);
  or CF (CF_OF_SF_ZF[3], adder_1_cout, subtractor_1_bout);
  Multiplexer #(.select(3), .width(8)) multiplexer_1 (
    .in0(adder_1_out), .in1(subtractor_1_out), .in2(or_1_out), .in3(and_1_out), .in4(not_1_out),
    .in5(shifter_1_out), .in6(shifter_2_out), .in7({8{1'b0}}), .out({CF_OF_SF_ZF[1], Res[6:0]}), .sel(ctrUAL));  // open: en
  and ZF (CF_OF_SF_ZF[0], ~Res[0], ~Res[1], ~Res[2], ~Res[3], ~Res[4], ~Res[5], ~Res[6], ~CF_OF_SF_ZF[1]);  // AND_Gate

  assign Res[7] = CF_OF_SF_ZF[1];
endmodule

module Decodeur (
  input  [3:0] ABCD,
  output [2:0] ctrUAL,
  output isJMP,
  output regWrite,
  output isLoad
);

  not not_1 (regWrite, ABCD[3]);
  and and_1 (isLoad, ~ABCD[3], ABCD[2], ABCD[1], ABCD[0]);  // AND_Gate

  assign ctrUAL = ABCD[2:0];
  assign isJMP = ABCD[3];
endmodule

module banc_registre (
  input  [7:0] valIn,
  input  [3:0] rs,
  input  [3:0] rd,
  input  [3:0] rt,
  input  reset,
  input  regWrite,
  input  clock,
  output [7:0] rs_2,
  output [7:0] rt_2
);

  wire and_1_out, and_2_out, and_3_out, and_4_out, and_5_out, and_6_out, and_7_out, and_8_out, and_9_out,
       and_10_out, and_11_out, and_12_out, and_13_out, and_14_out, and_15_out, and_16_out,
       select_registre_1_out_2, select_registre_1_out_3, select_registre_1_out_4, select_registre_1_out_5,
       select_registre_1_out_6, select_registre_1_out_7, select_registre_1_out_8, select_registre_1_out_9,
       select_registre_1_out_10, select_registre_1_out_11, select_registre_1_out_12,
       select_registre_1_out_13, select_registre_1_out_14, select_registre_1_out_15,
       select_registre_1_out_16, select_registre_1_out_17;
  wire [7:0] R1, R2, R3, R4, R5, R6, R7, R8, R9, R10, R11, R12, R13, R14, R15, R16;

  select_registre select_registre_1 (
    .rd(rd), .out_2(select_registre_1_out_2), .out_3(select_registre_1_out_3),
    .out_4(select_registre_1_out_4), .out_5(select_registre_1_out_5), .out_6(select_registre_1_out_6),
    .out_7(select_registre_1_out_7), .out_8(select_registre_1_out_8), .out_9(select_registre_1_out_9),
    .out_10(select_registre_1_out_10), .out_11(select_registre_1_out_11), .out_12(select_registre_1_out_12),
    .out_13(select_registre_1_out_13), .out_14(select_registre_1_out_14), .out_15(select_registre_1_out_15),
    .out_16(select_registre_1_out_16), .out_17(select_registre_1_out_17));
  and and_1 (and_1_out, regWrite, select_registre_1_out_2);
  and and_2 (and_2_out, regWrite, select_registre_1_out_6);
  and and_3 (and_3_out, regWrite, select_registre_1_out_10);
  and and_4 (and_4_out, regWrite, select_registre_1_out_14);
  Register register_1 (.D(valIn), .en(and_1_out), .Q(R1), .clk(clock), .clr(reset));
  Register register_2 (.D(valIn), .en(and_2_out), .Q(R5), .clk(clock), .clr(reset));
  Register register_3 (.D(valIn), .en(and_3_out), .Q(R9), .clk(clock), .clr(reset));
  Register register_4 (.D(valIn), .en(and_4_out), .Q(R13), .clk(clock), .clr(reset));
  and and_5 (and_5_out, regWrite, select_registre_1_out_3);
  and and_6 (and_6_out, regWrite, select_registre_1_out_7);
  and and_7 (and_7_out, regWrite, select_registre_1_out_11);
  and and_8 (and_8_out, regWrite, select_registre_1_out_15);
  Register register_5 (.D(valIn), .en(and_5_out), .Q(R2), .clk(clock), .clr(reset));
  Register register_6 (.D(valIn), .en(and_6_out), .Q(R6), .clk(clock), .clr(reset));
  Register register_7 (.D(valIn), .en(and_7_out), .Q(R10), .clk(clock), .clr(reset));
  Register register_8 (.D(valIn), .en(and_8_out), .Q(R14), .clk(clock), .clr(reset));
  Register register_9 (.D(valIn), .en(and_9_out), .Q(R3), .clk(clock), .clr(reset));
  and and_9 (and_9_out, regWrite, select_registre_1_out_4);
  Register register_10 (.D(valIn), .en(and_10_out), .Q(R7), .clk(clock), .clr(reset));
  and and_10 (and_10_out, regWrite, select_registre_1_out_8);
  Register register_11 (.D(valIn), .en(and_11_out), .Q(R11), .clk(clock), .clr(reset));
  and and_11 (and_11_out, regWrite, select_registre_1_out_12);
  Register register_12 (.D(valIn), .en(and_12_out), .Q(R15), .clk(clock), .clr(reset));
  and and_12 (and_12_out, regWrite, select_registre_1_out_16);
  and and_13 (and_13_out, regWrite, select_registre_1_out_5);
  and and_14 (and_14_out, regWrite, select_registre_1_out_9);
  and and_15 (and_15_out, regWrite, select_registre_1_out_13);
  and and_16 (and_16_out, regWrite, select_registre_1_out_17);
  Register register_13 (.D(valIn), .en(and_13_out), .Q(R4), .clk(clock), .clr(reset));
  Register register_14 (.D(valIn), .en(and_14_out), .Q(R8), .clk(clock), .clr(reset));
  Register register_15 (.D(valIn), .en(and_15_out), .Q(R12), .clk(clock), .clr(reset));
  Register register_16 (.D(valIn), .en(and_16_out), .Q(R16), .clk(clock), .clr(reset));
  Multiplexer #(.select(4), .width(8)) multiplexer_1 (
    .in0(R1), .in1(R2), .in2(R3), .in3(R4), .in4(R5), .in5(R6), .in6(R7), .in7(R8), .in8(R9), .in9(R10),
    .in10(R11), .in11(R12), .in12(R13), .in13(R14), .in14(R15), .in15(R16), .out(rs_2), .sel(rs));  // open: en
  Multiplexer #(.select(4), .width(8)) multiplexer_2 (
    .in0(R1), .in1(R2), .in2(R3), .in3(R4), .in4(R5), .in5(R6), .in6(R7), .in7(R8), .in8(R9), .in9(R10),
    .in10(R11), .in11(R12), .in12(R13), .in13(R14), .in14(R15), .in15(R16), .out(rt_2), .sel(rt));  // open: en

  // Other names for the same wires on the sheet: regW = regWrite
endmodule

module selection_registre (
  input  [3:0] rd_rs,
  input  [3:0] rs_rt,
  input  [3:0] rt,
  input  isJMP,
  output [3:0] rd,
  output [3:0] rs,
  output [3:0] rt_2
);

  wire not_1_out, not_2_out;

  Multiplexer #(.width(4)) multiplexer_1 (.in0(rd_rs), .in1(rs_rt), .out(rs), .sel(not_1_out));  // open: en
  not not_1 (not_1_out, isJMP);
  Multiplexer #(.width(4)) multiplexer_2 (.in0(rs_rt), .in1(rt), .out(rt_2), .sel(not_2_out));  // open: en
  not not_2 (not_2_out, isJMP);

  assign rd = rd_rs;
endmodule

module Nono_1 (
  input  in_1,
  input  Reset
);

  wire clock_1_out, decodeur_1_isload, isJMP, not_1_out, regWrite;
  wire [1:0] controle_saut_1_e0e1;
  wire [2:0] decodeur_1_ctrual;
  wire [3:0] opcode, selection_registre_1_rd, selection_registre_1_rs, selection_registre_1_rt_2,
       UAL_cf_of_sf_zf;
  wire [7:0] adder_1_out, adder_2_out, banc_registre_1_rs_2, banc_registre_1_rt_2, bit_extender_1_out,
       multiplexer_1_out, multiplexer_2_out, PC_q, UAL_res;
  wire [11:0] ram_1_data;

  Clock clock_1 (.out(clock_1_out));
  Register PC (.D(multiplexer_2_out), .en(1'b1), .Q(PC_q), .clk(clock_1_out), .clr(Reset));
  RAM #(.dataWidth(16)) ram_1 (
    .addr(PC_q), .data({opcode, ram_1_data}), .clk(clock_1_out), .ld(in_1));  // open: sel, clr
  Adder adder_1 (.a(PC_q), .b(8'h1), .out(adder_1_out));  // open: cin, cout
  selection_registre selection_registre_1 (
    .rd_rs(ram_1_data[3:0]), .rs_rt(ram_1_data[7:4]), .rt(ram_1_data[11:8]), .isJMP(isJMP),
    .rd(selection_registre_1_rd), .rs(selection_registre_1_rs), .rt_2(selection_registre_1_rt_2));
  assign bit_extender_1_out = {{4{1'b0}}, ram_1_data[3:0]};  // Bit_Extender bit_extender_1
  Multiplexer #(.width(8)) multiplexer_1 (
    .in0({ram_1_data[3:0], ram_1_data[3:0]}), .in1(UAL_res), .out(multiplexer_1_out), .sel(not_1_out));  // open: en
  not not_1 (not_1_out, decodeur_1_isload);
  Decodeur decodeur_1 (
    .ABCD(opcode), .isJMP(isJMP), .regWrite(regWrite), .isLoad(decodeur_1_isload), .ctrUAL(decodeur_1_ctrual));
  banc_registre banc_registre_1 (
    .valIn(multiplexer_1_out), .reset(Reset), .regWrite(regWrite), .clock(clock_1_out),
    .rd(selection_registre_1_rt_2), .rs(selection_registre_1_rs), .rt(selection_registre_1_rd),
    .rs_2(banc_registre_1_rs_2), .rt_2(banc_registre_1_rt_2));
  Adder adder_2 (.a(adder_1_out), .b(bit_extender_1_out), .out(adder_2_out));  // open: cin, cout
  Multiplexer #(.select(2), .width(8)) multiplexer_2 (
    .in0({8{1'b1}}), .in2(adder_2_out), .in3(adder_1_out), .out(multiplexer_2_out), .sel(controle_saut_1_e0e1));  // open: in1, en
  UAL UAL (
    .Rs(banc_registre_1_rs_2), .Rt(banc_registre_1_rt_2), .ctrUAL(decodeur_1_ctrual), .Res(UAL_res),
    .CF_OF_SF_ZF(UAL_cf_of_sf_zf));
  controle_saut controle_saut_1 (.opcode(opcode), .CF_OF_SF_ZF(UAL_cf_of_sf_zf), .e0e1(controle_saut_1_e0e1));

  // Notes on the sheet:
  //   Sélection
  //   registre
  //   Banc registre
  //   HALT
  //   Rs
  //   Rt
  //   saut
  //   instruction suivante
endmodule

module controle_saut (
  input  [3:0] opcode,
  input  [3:0] CF_OF_SF_ZF,
  output [1:0] e0e1
);

  wire and_1_out, and_2_out, and_3_out, and_4_out, and_5_out, not_1_out, not_2_out, not_3_out, not_4_out,
       not_5_out, not_6_out, not_7_out;

  not not_1 (not_1_out, opcode[0]);
  not not_2 (not_2_out, opcode[2]);
  not not_3 (not_3_out, CF_OF_SF_ZF[0]);
  not not_4 (not_4_out, opcode[2]);
  not not_5 (not_5_out, CF_OF_SF_ZF[0]);
  not not_6 (not_6_out, CF_OF_SF_ZF[0]);
  not not_7 (not_7_out, CF_OF_SF_ZF[1]);
  or or_1 (e0e1[0], opcode[2], opcode[1], opcode[0]);
  and and_1 (and_1_out, not_1_out, opcode[1], not_2_out, not_3_out);
  and and_2 (and_2_out, opcode[1], opcode[2], CF_OF_SF_ZF[0]);
  and and_3 (and_3_out, opcode[0], not_4_out, not_5_out, CF_OF_SF_ZF[1]);
  and and_4 (and_4_out, opcode[0], opcode[2], not_6_out, not_7_out);
  and and_5 (and_5_out, opcode[0], opcode[1], CF_OF_SF_ZF[0]);
  or or_2 (e0e1[1], and_1_out, and_2_out, and_3_out, and_4_out, and_5_out);

  // Notes on the sheet:
  //   00 : halt
  //   10 : saut
  //   11 : instruction suivante
endmodule

module select_registre (
  input  [3:0] rd,
  output out_2,
  output out_3,
  output out_4,
  output out_5,
  output out_6,
  output out_7,
  output out_8,
  output out_9,
  output out_10,
  output out_11,
  output out_12,
  output out_13,
  output out_14,
  output out_15,
  output out_16,
  output out_17
);

  and r0 (out_2, ~rd[0], ~rd[1], ~rd[2], ~rd[3]);  // AND_Gate
  and r1 (out_3, rd[0], ~rd[1], ~rd[2], ~rd[3]);  // AND_Gate
  and r2 (out_4, ~rd[0], rd[1], ~rd[2], ~rd[3]);  // AND_Gate
  and r3 (out_5, rd[0], rd[1], ~rd[2], ~rd[3]);  // AND_Gate
  and r4 (out_6, ~rd[0], ~rd[1], rd[2], ~rd[3]);  // AND_Gate
  and r6 (out_8, ~rd[0], rd[1], rd[2], ~rd[3]);  // AND_Gate
  and r5 (out_7, rd[0], ~rd[1], rd[2], ~rd[3]);  // AND_Gate
  and r7 (out_9, rd[0], rd[1], rd[2], ~rd[3]);  // AND_Gate
  and r8 (out_10, ~rd[0], ~rd[1], ~rd[2], rd[3]);  // AND_Gate
  and r10 (out_12, ~rd[0], rd[1], ~rd[2], rd[3]);  // AND_Gate
  and r9 (out_11, rd[0], ~rd[1], ~rd[2], rd[3]);  // AND_Gate
  and r11 (out_13, rd[0], rd[1], ~rd[2], rd[3]);  // AND_Gate
  and r12 (out_14, ~rd[0], ~rd[1], rd[2], rd[3]);  // AND_Gate
  and r13 (out_15, rd[0], ~rd[1], rd[2], rd[3]);  // AND_Gate
  and r14 (out_16, ~rd[0], rd[1], rd[2], rd[3]);  // AND_Gate
  and r15 (out_17, rd[0], rd[1], rd[2], rd[3]);
endmodule

module test (
  input  A,
  input  B,
  input  C,
  input  D,
  output isJMP,
  output isLoad
);

  wire not_1_out;

  not not_1 (not_1_out, A);
  or or_1 (isJMP, not_1_out, D, C);
endmodule
